// Logisim project guia0606.circ as structural Verilog: 2 circuits, main circuit main
module normalFunction (
  input  x,
  input  y,
  input  w,
  input  z,
  output out_5
);

  wire and_1_out, and_2_out, and_3_out, not_1_out, not_2_out, not_3_out, not_4_out, not_5_out, not_6_out,
       not_7_out, or_1_out, or_2_out;

  not not_1 (not_1_out, y);
  or or_1 (or_1_out, not_1_out, w, not_2_out);
  not not_2 (not_2_out, x);
  and and_1 (and_1_out, y, not_3_out, x);
  not not_3 (not_3_out, w);
  and and_2 (and_2_out, z, w, y);
  not not_4 (not_4_out, x);
  not not_5 (not_5_out, or_1_out);
  and and_3 (and_3_out, not_5_out, not_6_out);
  not not_6 (not_6_out, and_1_out);
  or or_2 (or_2_out, and_2_out, not_4_out);
  not not_7 (not_7_out, or_2_out);
  or or_3 (out_5, and_3_out, not_7_out);
endmodule

module main (
  input  x,
  input  y,
  input  w,
  input  z,
  output out_5
);

  wire normalfunction_1_out_5;

  normalFunction normalfunction_1 (.out_5(normalfunction_1_out_5));  // open: x, y, w, z
  not xnor_1 (out_5, normalfunction_1_out_5);  // XNOR_Gate
endmodule
